# Fritzing sketch button_and_led (saved by Fritzing 0.9.6b)
breadboards: 1

parts:
  IC5 = DIP - 28 pins [chip_label=IC package="DIP (Dual Inline) [THT]"]
  R2 = Resistor [tolerance=±5% resistance=10k package=THT]
  S2 = Pushbutton [package="[SMD]"]
  LED2 = smd LED [color="Red (633nm)" package="0805 [SMD]"]
  R1 = Resistor [tolerance=±5% resistance=330 package="0805 [SMD]"]

nets:
  N1: IC5.GND, R2.Pin_0, R1.Pin_0
  N2: IC5.3V3, S2.Pin_1, S2.Pin_2
  N3: IC5.P13, R2.Pin_1, S2.Pin_3, S2.Pin_4, LED2.anode
  N4: LED2.cathode, R1.Pin_1

custom parts:
  DIP - 28 pins: A DIP stand-in part for whatever IC you want. With 28 pins on a 300mil dual inline package (DIP) footprint.
